# Fritzing sketch domohome_v1_breadboard (saved by Fritzing 0.9.3b)

parts:
  Raspberry_Pi1 = Raspberry Pi 2
  KY-2 = Keyes Relay [package=THT]
  KY-3 = Keyes Relay [package=THT]
  DHT22 = DHT22 Humidity and Temperature Sensor
  Foto_relé = S1133 Si Photodiode [package="8mm Ceramic [THT]"]
  R3 = Resistor [tolerance=±5% resistance=220 package="2512 [SMD]"]
  Sensor_puerta = Toggle Switch [package=THT]
  Sensor_de_lluvia = Pushbutton [package="[THT]"]
  Anemómetro = Pushbutton [package="[THT]"]

nets:
  3V3: Raspberry_Pi1.3v3, Raspberry_Pi1.3V3, DHT22.VDD, Sensor_puerta.L2
  N1: Raspberry_Pi1.GPIO4, DHT22.DATA
  GND: Raspberry_Pi1.GND, Raspberry_Pi1.GPIO13, Raspberry_Pi1.GPIO23, KY-2.ground, KY-3.ground, DHT22.GND, Foto_relé.cathode, R3.Pin_0, Sensor_de_lluvia.Pin_3, Sensor_de_lluvia.Pin_4, Anemómetro.Pin_3, Anemómetro.Pin_4
  N2: Raspberry_Pi1.GPIO5, Foto_relé.anode
  N3: Raspberry_Pi1.GPIO6, KY-3.power
  N4: Raspberry_Pi1.GPIO19, KY-2.power
  N5: Raspberry_Pi1.GPIO18, R3.Pin_1, Sensor_puerta.COM
  N6: Raspberry_Pi1.5V, KY-2.signal, KY-3.signal

custom parts:
  Keyes Relay: The Keyes 5V relay module is suitable for SCM development, home appliance control. It uses a 5V~12V TIL control signal which can control DC / AC signal.
